// Digital circuit boot_rom.dig as structural Verilog
module boot_rom (
  input  [23:0] Addr,
  input  En,
  output [31:0] Out_code
);

  ROM #(.AddrBits(24), .Bits(8)) Boot_B0 (.A({2'b00, Addr[23:2]}), .sel(En), .D(Out_code[7:0]));
  ROM #(.AddrBits(24), .Bits(8)) Boot_B1 (.A({2'b00, Addr[23:2]}), .sel(En), .D(Out_code[15:8]));
  ROM #(.AddrBits(24), .Bits(8)) Boot_B2 (.A({2'b00, Addr[23:2]}), .sel(En), .D(Out_code[23:16]));
  ROM #(.AddrBits(24), .Bits(8)) Boot_B3 (.A({2'b00, Addr[23:2]}), .sel(En), .D(Out_code[31:24]));

  // Notes on the sheet:
  //   contents of Boot_B0 (hex, n*v repeats v):
  //   7f,37,b7,37,13,83,23,13,93,e3,b7,37,b7,37,97,e7
  //   contents of Boot_B1 (hex, n*v repeats v):
  //   0,3,3,1e,e,45,80,3,83,e8,2,3,3,e,0,80
  //   contents of Boot_B2 (hex, n*v repeats v):
  //   4*0,e,3,b3,13,13,c3,5*0,80
  //   contents of Boot_B3 (hex, n*v repeats v):
  //   80,40,2,2,80,4*0,ff,4*0,82,fc
endmodule
