// Digital circuit main.dig as structural Verilog
module main (
  input  Clock
);

  wire addrflag_boot, addrflag_memtmp, alu_op, csr_op, cust_ctrl_1_pc_init, Cust_op, imm_7, imm_12, imm_20,
       Invalid_op, jmp_op, mechine_op, mem_op, rd, rs1, rs2;
  wire [23:0] addr_real;
  wire [30:24] program_counter_1_pc_exec;
  wire [31:0] instruction_code;

  cust_ctrl cust_ctrl_1 (.op_code(instruction_code), .cust_code(Cust_op), .Clock(Clock), .PC_init(cust_ctrl_1_pc_init));
  program_counter program_counter_1 (
    .PC_inited(cust_ctrl_1_pc_init), .En(1'b1), .Clock(Clock), .Addr_jmp({32{1'b0}}), .En_jmp(1'b0),
    .PC_exec({addrflag_boot, program_counter_1_pc_exec[30:26], addrflag_memtmp, program_counter_1_pc_exec[24], addr_real}));  // open: PC_next
  // instruction_decoder instruction_decoder_1: pin names not known; wires that end beside it: instruction_code, 1'b1, rd, rs1, rs2, imm_7, imm_20, imm_12, Invalid_op, mechine_op, csr_op, jmp_op, alu_op, mem_op, Cust_op
  boot_rom boot_rom_1 (.Addr(addr_real), .En(addrflag_boot), .Out_code(instruction_code));

  // Other names for the same wires on the sheet: c = Clock

  // Notes on the sheet:
  //   Clock: Hz: 50000
endmodule
